// Logisim project Guia_0401_a.circ as structural Verilog: 1 circuit, main circuit main
module main (
  input  x,
  input  y,
  input  z,
  output Saida
);

  wire not_1_out, not_2_out, or_1_out;

  not not_1 (not_1_out, y);
  or or_1 (or_1_out, not_1_out, z);
  not not_2 (not_2_out, or_1_out);
  and and_1 (Saida, x, not_2_out);
endmodule
