// Logisim project Guia_0402_d03.circ as structural Verilog: 1 circuit, main circuit main
module main (
  input  x,
  input  y,
  output z
);

  wire not_1_out;

  not not_1 (not_1_out, x);
  or or_1 (z, not_1_out, y);
endmodule
