// Logisim project Guia_0403_c.circ as structural Verilog: 1 circuit, main circuit main
module main (
  input  x,
  input  y,
  input  z,
  input  w,
  output s
);

  wire and_1_out, and_2_out, and_3_out, and_4_out, and_5_out, and_6_out, and_7_out, not_1_out, not_2_out,
       not_3_out, not_4_out, not_5_out, not_6_out, not_7_out, not_8_out, not_9_out, not_10_out, not_11_out,
       not_12_out;

  not not_1 (not_1_out, x);
  not not_2 (not_2_out, y);
  not not_3 (not_3_out, w);
  not not_4 (not_4_out, x);
  not not_5 (not_5_out, y);
  not not_6 (not_6_out, z);
  not not_7 (not_7_out, x);
  not not_8 (not_8_out, w);
  not not_9 (not_9_out, x);
  not not_10 (not_10_out, z);
  not not_11 (not_11_out, x);
  not not_12 (not_12_out, w);
  and and_1 (and_1_out, not_1_out, not_2_out, not_3_out, z);
  and and_2 (and_2_out, not_4_out, not_5_out, w, not_6_out);
  and and_3 (and_3_out, not_7_out, y, not_8_out, z);
  and and_4 (and_4_out, not_9_out, y, w, not_10_out);
  and and_5 (and_5_out, not_11_out, y, w, z);
  and and_6 (and_6_out, x, y, not_12_out, z);
  and and_7 (and_7_out, x, y, w, z);
  or or_1 (s, and_1_out, and_2_out, and_3_out, and_4_out, and_5_out, and_6_out, and_7_out);
endmodule
