// Logisim project Guia_0405_b_PoS.circ as structural Verilog: 1 circuit, main circuit main
module main (
  input  x,
  input  y,
  output s
);

  wire not_1_out, or_1_out, or_2_out;

  not not_1 (not_1_out, x);
  or or_1 (or_1_out, x, y);
  or or_2 (or_2_out, not_1_out, y);
  and and_1 (s, or_1_out, or_2_out);
endmodule
