// Logisim project Guia_0804.circ as structural Verilog: 1 circuit, main circuit main
module main (
  input  a0,
  input  b0,
  input  a1,
  input  b1,
  output out_5
);

  wire and_1_out, and_2_out, not_1_out, not_2_out, not_3_out, not_4_out;

  not not_1 (not_1_out, a0);
  not not_2 (not_2_out, b0);
  not not_3 (not_3_out, a1);
  not not_4 (not_4_out, b1);
  and and_1 (and_1_out, a0, a1);
  and and_2 (and_2_out, b0, b1);
  or or_1 (out_5, and_1_out, and_2_out);
endmodule
