// Logisim project ED_1102.circ as structural Verilog: 2 circuits, main circuit main
module main (
  input  input__ou_x,
  input  clear,
  output \output 
);

  wire clock_out, d_ff_1_q, d_ff_2_q, d_ff_2_qn, d_ff_3_q, d_ff_4_q;

  Clock clock (.out(clock_out));
  D_Flip_Flop d_ff_1 (.clk(clock_out), .D(input__ou_x), .Q(d_ff_1_q), .reset(clear));  // open: Qn, preset
  D_Flip_Flop d_ff_2 (.clk(clock_out), .D(d_ff_1_q), .Q(d_ff_2_q), .Qn(d_ff_2_qn), .reset(clear));  // open: preset
  D_Flip_Flop d_ff_3 (.clk(clock_out), .D(d_ff_2_q), .Q(d_ff_3_q), .reset(clear));  // open: Qn, preset
  D_Flip_Flop d_ff_4 (.clk(clock_out), .D(d_ff_3_q), .Q(d_ff_4_q), .reset(clear));  // open: Qn, preset
  and and_1 (\output , d_ff_1_q, d_ff_2_qn, d_ff_3_q, d_ff_4_q);
endmodule

module mealy_1110 (
  input  input__ou_x,
  input  clear,
  output \output 
);

  wire clock_out, d_ff_1_q, d_ff_2_q, d_ff_2_qn, d_ff_3_q;

  Clock clock (.out(clock_out));
  D_Flip_Flop d_ff_1 (.clk(clock_out), .D(input__ou_x), .Q(d_ff_1_q), .reset(clear));  // open: Qn, preset
  D_Flip_Flop d_ff_2 (.clk(clock_out), .D(d_ff_1_q), .Q(d_ff_2_q), .Qn(d_ff_2_qn), .reset(clear));  // open: preset
  D_Flip_Flop d_ff_3 (.clk(clock_out), .D(d_ff_2_q), .Q(d_ff_3_q), .reset(clear));  // open: Qn, preset
  D_Flip_Flop d_ff_4 (.clk(clock_out), .D(d_ff_3_q), .reset(clear));  // open: Q, Qn, preset
  and and_1 (\output , d_ff_1_q, d_ff_2_qn, d_ff_3_q, input__ou_x);
endmodule
