// Logisim project ED13.circ as structural Verilog
module ed1302 (
  input  in_1,
  input  clear,
  output [4:0] out_3
);

  wire clock_1_out;

  Clock clock_1 (.out(clock_1_out));
  J_K_Flip_Flop #(.trigger("falling"), .Pre_Clr_Positions("LEGACY"), .enable("true"), .NewFFLayout("false")) j_k_ff_1 (
    .J(in_1), .clk(clock_1_out), .K(in_1), .Q(in_1), .reset(clear));  // open: Qn, preset, en
  J_K_Flip_Flop #(.trigger("falling"), .Pre_Clr_Positions("LEGACY"), .enable("true"), .NewFFLayout("false")) j_k_ff_2 (
    .J(in_1), .clk(in_1), .K(in_1), .Q(out_3[1]), .reset(clear));  // open: Qn, preset, en
  J_K_Flip_Flop #(.trigger("falling"), .Pre_Clr_Positions("LEGACY"), .enable("true"), .NewFFLayout("false")) j_k_ff_3 (
    .J(in_1), .clk(out_3[1]), .K(in_1), .Q(out_3[2]), .reset(clear));  // open: Qn, preset, en
  J_K_Flip_Flop #(.trigger("falling"), .Pre_Clr_Positions("LEGACY"), .enable("true"), .NewFFLayout("false")) j_k_ff_4 (
    .J(in_1), .clk(out_3[2]), .K(in_1), .Q(out_3[3]), .reset(clear));  // open: Qn, preset, en
  J_K_Flip_Flop #(.trigger("falling"), .Pre_Clr_Positions("LEGACY"), .enable("true"), .NewFFLayout("false")) j_k_ff_5 (
    .J(in_1), .clk(out_3[3]), .K(in_1), .Q(out_3[4]), .reset(clear));  // open: Qn, preset, en

  assign out_3[0] = in_1;
endmodule

module ed1301 (
  input  j,
  input  clear
);

  wire clock_1_out, j_k_ff_2_q, j_k_ff_3_q, j_k_ff_4_q, j_k_ff_5_q;

  Clock clock_1 (.out(clock_1_out));
  J_K_Flip_Flop #(.Pre_Clr_Positions("LEGACY"), .enable("true"), .NewFFLayout("false")) j_k_ff_1 (
    .J(1'b1), .clk(j_k_ff_2_q), .K(1'b1), .reset(clear));  // open: Q, Qn, preset, en
  J_K_Flip_Flop #(.Pre_Clr_Positions("LEGACY"), .enable("true"), .NewFFLayout("false")) j_k_ff_2 (
    .J(1'b1), .clk(j_k_ff_3_q), .K(1'b1), .Q(j_k_ff_2_q), .reset(clear));  // open: Qn, preset, en
  J_K_Flip_Flop #(.Pre_Clr_Positions("LEGACY"), .enable("true"), .NewFFLayout("false")) j_k_ff_3 (
    .J(1'b1), .clk(j_k_ff_4_q), .K(1'b1), .Q(j_k_ff_3_q), .reset(clear));  // open: Qn, preset, en
  J_K_Flip_Flop #(.Pre_Clr_Positions("LEGACY"), .enable("true"), .NewFFLayout("false")) j_k_ff_4 (
    .J(1'b1), .clk(j_k_ff_5_q), .K(1'b1), .Q(j_k_ff_4_q), .reset(clear));  // open: Qn, preset, en
  J_K_Flip_Flop #(.Pre_Clr_Positions("LEGACY"), .enable("true"), .NewFFLayout("false")) j_k_ff_5 (
    .J(1'b1), .clk(clock_1_out), .K(1'b1), .Q(j_k_ff_5_q), .reset(clear));  // open: Qn, preset, en
endmodule

module ed1303 (
  input  in_1,
  output [5:0] out_2
);

  wire and_1_out, and_2_out, and_3_out, and_4_out, and_5_out, clock_1_out, j_k_ff_1_qn, j_k_ff_2_qn,
       j_k_ff_3_qn, j_k_ff_4_qn, j_k_ff_5_qn, nand_1_out, nand_2_out, not_1_out, not_2_out, not_3_out;

  Clock clock_1 (.out(clock_1_out));
  nand nand_1 (nand_1_out, and_2_out, and_4_out);
  nand nand_2 (nand_2_out, in_1, nand_1_out);
  not not_1 (not_1_out, out_2[0]);
  and and_1 (and_1_out, not_1_out, out_2[1]);
  and and_2 (and_2_out, and_1_out, and_3_out);
  not not_2 (not_2_out, out_2[2]);
  and and_3 (and_3_out, not_2_out, out_2[3]);
  and and_4 (and_4_out, and_3_out, and_5_out);
  not not_3 (not_3_out, out_2[4]);
  and and_5 (and_5_out, not_3_out, out_2[5]);
  J_K_Flip_Flop #(.Pre_Clr_Positions("LEGACY"), .enable("true"), .NewFFLayout("false")) j_k_ff_1 (
    .J(1'b1), .clk(clock_1_out), .K(1'b1), .Q(out_2[0]), .Qn(j_k_ff_1_qn), .reset(nand_2_out));  // open: preset, en
  J_K_Flip_Flop #(.Pre_Clr_Positions("LEGACY"), .enable("true"), .NewFFLayout("false")) j_k_ff_2 (
    .J(1'b1), .clk(j_k_ff_1_qn), .K(1'b1), .Q(out_2[1]), .Qn(j_k_ff_2_qn), .reset(nand_2_out));  // open: preset, en
  J_K_Flip_Flop #(.Pre_Clr_Positions("LEGACY"), .enable("true"), .NewFFLayout("false")) j_k_ff_3 (
    .J(1'b1), .clk(j_k_ff_2_qn), .K(1'b1), .Q(out_2[2]), .Qn(j_k_ff_3_qn), .reset(nand_2_out));  // open: preset, en
  J_K_Flip_Flop #(.Pre_Clr_Positions("LEGACY"), .enable("true"), .NewFFLayout("false")) j_k_ff_4 (
    .J(1'b1), .clk(j_k_ff_3_qn), .K(1'b1), .Q(out_2[3]), .Qn(j_k_ff_4_qn), .reset(nand_2_out));  // open: preset, en
  J_K_Flip_Flop #(.Pre_Clr_Positions("LEGACY"), .enable("true"), .NewFFLayout("false")) j_k_ff_5 (
    .J(1'b1), .clk(j_k_ff_4_qn), .K(1'b1), .Q(out_2[4]), .Qn(j_k_ff_5_qn), .reset(nand_2_out));  // open: preset, en
  J_K_Flip_Flop #(.Pre_Clr_Positions("LEGACY"), .enable("true"), .NewFFLayout("false")) j_k_ff_6 (
    .J(1'b1), .clk(j_k_ff_5_qn), .K(1'b1), .Q(out_2[5]), .reset(nand_2_out));  // open: Qn, preset, en
endmodule
