// Logisim project Guia_0601d.circ as structural Verilog: 1 circuit, main circuit main
module main (
  input  x,
  input  y,
  input  z,
  output p3
);

  wire and_1_out, and_2_out, and_3_out, not_1_out, not_2_out, not_3_out, or_1_out, or_2_out;

  not not_1 (not_1_out, y);
  not not_2 (not_2_out, x);
  not not_3 (not_3_out, z);
  and and_1 (and_1_out, not_2_out, not_1_out);
  or or_1 (or_1_out, z, y);
  or or_2 (or_2_out, not_3_out, x);
  and and_2 (and_2_out, and_1_out, or_1_out);
  and and_3 (and_3_out, and_2_out, or_2_out);
  and and_4 (p3, and_3_out, not_3_out);

  // Notes on the sheet:
  //   ERRO: 001, 010, 100, 110$Erro na parte 1?
  //   p1
  //   p2
endmodule
