// Logisim project Guia_0603a.circ as structural Verilog: 1 circuit, main circuit main
module main (
  input  x,
  input  y,
  input  w,
  input  z
);

  wire and_1_out, and_2_out, and_3_out, and_4_out, and_5_out, and_6_out, and_7_out, and_8_out, and_9_out,
       and_10_out, not_1_out, not_2_out, not_3_out, not_4_out, or_1_out, or_2_out, or_3_out, or_4_out;

  not not_1 (not_1_out, y);
  not not_2 (not_2_out, x);
  not not_3 (not_3_out, w);
  not not_4 (not_4_out, z);
  and and_1 (and_1_out, not_2_out, not_3_out);
  and and_2 (and_2_out, and_1_out, or_1_out);
  or or_1 (or_1_out, z, y);
  and and_3 (and_3_out, not_3_out, z);
  or or_2 (or_2_out, and_3_out, and_4_out);
  and and_4 (and_4_out, not_2_out, not_1_out);
  and and_5 (and_5_out, w, not_4_out);
  or or_3 (or_3_out, and_5_out, and_6_out);
  and and_6 (and_6_out, x, not_1_out);
  and and_7 (and_7_out, x, not_1_out);
  or or_4 (or_4_out, and_7_out, and_8_out);
  and and_8 (and_8_out, not_3_out, not_4_out);
  and and_9 (and_9_out, x, y);
  and and_10 (and_10_out, w, not_4_out);
  // AND_Gate and_11 has open pins: in0=and_2_out, in1=or_2_out, out=open
  // AND_Gate and_12 has open pins: in0=or_3_out, in1=or_4_out, out=open
  // AND_Gate and_13 is placed but not wired
  // AND_Gate and_14 is placed but not wired
endmodule
