// Logisim project Guia_0603c.circ as structural Verilog: 1 circuit, main circuit main
module main (
  input  x,
  input  y,
  input  w,
  input  z,
  output out_5
);

  wire and_1_out, and_2_out, and_3_out, and_4_out, and_5_out, and_7_out, and_9_out, and_11_out, and_12_out,
       not_1_out, not_2_out, not_3_out, not_4_out, or_1_out, undriven;

  not not_1 (not_1_out, y);
  not not_2 (not_2_out, x);
  not not_3 (not_3_out, z);
  not not_4 (not_4_out, w);
  and and_1 (and_1_out, not_2_out, not_1_out);
  and and_2 (and_2_out, and_1_out, not_4_out);
  and and_3 (and_3_out, not_1_out, w);
  and and_4 (and_4_out, and_3_out, not_3_out);
  and and_5 (and_5_out, x, not_1_out);
  // AND_Gate and_6 has open pins: in0=and_5_out, in1=w, out=open
  and and_7 (and_7_out, x, not_4_out);
  // AND_Gate and_8 has open pins: in0=and_7_out, in1=z, out=open
  and and_9 (and_9_out, y, w);
  // AND_Gate and_10 has open pins: in0=and_9_out, in1=z, out=open
  or or_1 (or_1_out, and_2_out, and_4_out);
  buf and_11 (and_11_out, or_1_out);  // AND_Gate
  buf and_12 (and_12_out, undriven);  // AND_Gate
  and and_13 (out_5, and_11_out, and_12_out);
endmodule
