// Logisim project Guia_0701.circ as structural Verilog: 1 circuit, main circuit main
module main (
  input  a,
  input  b,
  input  sel,
  output out_4
);

  wire and_1_out, and_2_out, and_3_out, nand_1_out, not_1_out, not_2_out, not_3_out;

  not not_1 (not_1_out, b);
  not not_2 (not_2_out, a);
  not not_3 (not_3_out, sel);
  and and_1 (and_1_out, a, b);
  nand nand_1 (nand_1_out, a, b);
  and and_2 (and_2_out, nand_1_out, not_3_out);
  and and_3 (and_3_out, and_1_out, sel);
  or or_1 (out_4, and_2_out, and_3_out);
endmodule
