// Logisim project Guia_0402_c01.circ as structural Verilog: 1 circuit, main circuit main
module main (
  input  x,
  input  y,
  output out_3
);

  wire and_1_out, not_1_out, not_2_out, or_1_out;

  or or_1 (or_1_out, x, y);
  not not_1 (not_1_out, x);
  not not_2 (not_2_out, and_1_out);
  and and_1 (and_1_out, not_1_out, y);
  and and_2 (out_3, not_2_out, or_1_out);
endmodule
