// Logisim project Guia_0404_a.circ as structural Verilog: 1 circuit, main circuit main
module main (
  input  X,
  input  Y,
  input  Z,
  output s
);

  wire not_1_out, not_2_out, not_3_out, not_4_out, not_5_out, not_6_out, not_7_out, not_8_out, or_1_out,
       or_2_out, or_3_out, or_4_out;

  not not_1 (not_1_out, Z);
  not not_2 (not_2_out, Y);
  not not_3 (not_3_out, Z);
  not not_4 (not_4_out, X);
  not not_5 (not_5_out, Z);
  not not_6 (not_6_out, X);
  not not_7 (not_7_out, Y);
  not not_8 (not_8_out, Z);
  or or_1 (or_1_out, X, Y, not_1_out);
  or or_2 (or_2_out, X, not_2_out, not_3_out);
  or or_3 (or_3_out, not_4_out, Y, not_5_out);
  or or_4 (or_4_out, not_6_out, not_7_out, not_8_out);
  and and_1 (s, or_1_out, or_2_out, or_3_out, or_4_out);
endmodule
