// Logisim project Guia_0404_e.circ as structural Verilog: 1 circuit, main circuit main
module main (
  input  X,
  input  Y,
  input  W,
  input  Z,
  output S
);

  wire and_1_out, and_2_out, and_3_out, and_4_out, not_1_out, not_2_out, not_3_out, not_4_out, not_5_out;

  and and_1 (and_1_out, X, not_1_out);
  not not_1 (not_1_out, W);
  and and_2 (and_2_out, X, not_2_out);
  not not_2 (not_2_out, Z);
  not not_3 (not_3_out, X);
  and and_3 (and_3_out, not_3_out, Y, W);
  not not_4 (not_4_out, X);
  and and_4 (and_4_out, not_4_out, Y, not_5_out);
  not not_5 (not_5_out, Z);
  or or_1 (S, and_1_out, and_2_out, and_3_out, and_4_out);
endmodule
