// Logisim project Guia_0401_a_2.circ as structural Verilog: 1 circuit, main circuit main
module main (
  input  x,
  input  y,
  input  z,
  output out_4
);

  wire and_2_out, not_1_out;

  not not_1 (not_1_out, z);
  and and_1 (out_4, x, and_2_out);
  and and_2 (and_2_out, y, not_1_out);
endmodule
