// Logisim project Guia_0402_a01.circ as structural Verilog: 2 circuits, main circuit main
module main (
  input  x,
  input  y,
  input  z,
  output s
);
endmodule

module Guia_0402_a (
  input  x,
  input  y,
  output s
);

  wire nor_1_out, not_1_out, not_2_out;

  not not_1 (not_1_out, y);
  not not_2 (not_2_out, x);
  nor nor_1 (nor_1_out, x, not_1_out);
  and and_1 (s, not_2_out, nor_1_out);
endmodule
