// Logisim project Guia_0402_a02.circ as structural Verilog: 2 circuits, main circuit main
module main (
  input  x,
  input  y,
  input  z,
  output s
);
endmodule

module Guia_0402_a (
  input  x,
  input  y,
  output s
);

  wire not_1_out;

  not not_1 (not_1_out, x);
  and and_1 (s, not_1_out, y);
endmodule
