// Logisim project Guia_0402_b01.circ as structural Verilog: 2 circuits, main circuit main
module main (
  input  x,
  input  y,
  output out_3
);

  wire and_1_out, not_1_out, or_1_out;

  and and_1 (and_1_out, y, not_1_out);
  not not_1 (not_1_out, x);
  or or_1 (or_1_out, x, y);
  or or_2 (out_3, and_1_out, or_1_out);
endmodule

module Guia_0402_b02 (
  input  x,
  input  y,
  output s
);

  wire and_1_out, not_1_out;

  not not_1 (not_1_out, x);
  and and_1 (and_1_out, y, not_1_out);
  or or_1 (s, y, x, and_1_out);
endmodule
