// Logisim project Guia_0402_b02.circ as structural Verilog: 2 circuits, main circuit main
module main (
  input  x,
  input  y,
  output s
);
endmodule

module Guia_0402_b02 (
  input  x,
  input  y,
  output s
);

  wire and_1_out, not_1_out;

  not not_1 (not_1_out, x);
  and and_1 (and_1_out, not_1_out, y);
  or or_1 (s, x, y, and_1_out);
endmodule
