// Logisim project Guia_0404_d.circ as structural Verilog: 1 circuit, main circuit main
module main (
  input  X,
  input  Y,
  input  W,
  input  Z,
  output S
);

  wire and_1_out, and_2_out, and_3_out, and_4_out, and_5_out, not_1_out, not_2_out, not_3_out, not_4_out,
       not_5_out, not_6_out, not_7_out, not_8_out;

  not not_1 (not_1_out, X);
  not not_2 (not_2_out, Y);
  not not_3 (not_3_out, W);
  not not_4 (not_4_out, Z);
  not not_5 (not_5_out, X);
  not not_6 (not_6_out, Y);
  not not_7 (not_7_out, W);
  not not_8 (not_8_out, Z);
  and and_1 (and_1_out, Y, Z);
  and and_2 (and_2_out, X, Z);
  and and_3 (and_3_out, not_1_out, not_2_out, not_3_out, not_4_out);
  and and_4 (and_4_out, not_5_out, not_6_out, W, Z);
  and and_5 (and_5_out, X, Y, not_7_out, not_8_out);
  or or_1 (S, and_1_out, and_2_out, and_3_out, and_4_out, and_5_out);
endmodule
