// Logisim project Guia_0805.circ as structural Verilog: 2 circuits, main circuit main
module main (
  input  [4:0] in_1,
  output out_2,
  output [4:0] out_3
);

  wire [4:0] not_1_out;

  assign not_1_out = ~in_1;  // NOT_Gate not_1, 5 bits wide
  Adder #(.width(5)) adder_1 (.a(not_1_out), .b(5'b00001), .out(out_3), .cout(out_2));  // open: cin
endmodule

module complemento_1 (
  input  [4:0] a,
  output [4:0] out_2
);

  assign out_2 = ~a;  // NOT_Gate not_1, 5 bits wide
endmodule
